# Fritzing sketch Solenoid_Controller (saved by Fritzing 0.9.5d)
breadboards: 1

parts:
  Mod1 = Raspberry Pi Pico W
  U1 = LIPO-1000mAh [package=lipo-1000]
  R1 = Resistor [tolerance=±5% resistance=5 package=THT]
  R2 = Resistor [tolerance=±5% resistance=5 package=THT]
  Part1 = Soil Moisture Sensor
  S1 = H-Bridge with L298N
  L1 = Solenoid
  N_Mosfet = Basic FET N-Channel [package="TO220 [THT]"]
  R3 = Resistor [tolerance=±5% resistance=220 package="2512 [SMD]"]
  VCC1 = Battery block 9V
  R4 = Resistor [tolerance=±5% resistance=220 package=THT]
  R5 = Resistor [tolerance=±5% resistance=220 package=THT]

nets (from the breadboard view):
  GND: Mod1.pin_3, Mod1.pin_8, Mod1.pin_13, Mod1.pin_18, Mod1.pin_23, Mod1.pin_28, Mod1.pin_33, Mod1.pin_38, Mod1.pin_42, U1.-, R2.Pin_1, Part1.GND, S1.GND, R3.Pin_0, VCC1.-
  N1: Mod1.pin_17, R5.Pin_1
  N2: Mod1.pin_19, R4.Pin_1
  N3: Mod1.pin_21, N_Mosfet.source, R3.Pin_1
  N4: Mod1.pin_31, R1.Pin_0, R2.Pin_0
  N5: Mod1.pin_34, Part1.SIG
  N6: Mod1.pin_36, Part1.VCC, N_Mosfet.gate
  N7: Mod1.pin_39, U1.+, R1.Pin_1
  N8: S1.12V, VCC1.+
  N9: S1.5V, N_Mosfet.drain
  N10: S1.ENB, S1.ENB-5V
  N11: S1.M2-01, L1.pin2
  N12: S1.M2-02, L1.pin1

custom parts:
  Raspberry Pi Pico W: Raspberry Pi Pico W. Based around the RP2040 microcontroller the Pico W is a low cost microcontroller device bringing Raspberry Pi quality, cost, and easy of use to the microcontroller space. The areas marked KEEPOUT in pcb silkscreen should not have traces running through them to avoid shorts on a soldered in module!
  H-Bridge with L298N: h-bridge
