# Fritzing sketch moisture_sensor (saved by Fritzing 0.9.5d)
breadboards: 1

parts:
  Mod1 = Raspberry Pi Pico W
  U2 = LIPO-1000mAh [package=lipo-1000]
  Part2 = Soil Moisture Sensor
  R3 = Resistor [tolerance=±5% resistance=5 package=THT]
  R4 = Resistor [tolerance=±5% resistance=5 package=THT]

nets:
  N1: Mod1.pin_3, Mod1.pin_8, Mod1.pin_13, Mod1.pin_18, Mod1.pin_23, Mod1.pin_28, Mod1.pin_33, Mod1.pin_38, Mod1.pin_42, U2.-, Part2.GND, R3.Pin_1
  N2: Mod1.pin_31, R3.Pin_0, R4.Pin_0
  N3: Mod1.pin_34, Part2.SIG
  N4: Mod1.pin_36, Part2.VCC
  N5: Mod1.pin_39, U2.+, R4.Pin_1

custom parts:
  Raspberry Pi Pico W: Raspberry Pi Pico W. Based around the RP2040 microcontroller the Pico W is a low cost microcontroller device bringing Raspberry Pi quality, cost, and easy of use to the microcontroller space. The areas marked KEEPOUT in pcb silkscreen should not have traces running through them to avoid shorts on a soldered in module!
